// Logisim project 1.circ as structural Verilog: 1 circuit, main circuit alu8
module alu8 (
  input  [7:0] a,
  input  [7:0] b,
  input  [3:0] op,
  output [7:0] rddata
);

  wire and_11_out, and_12_out, and_13_out, and_14_out, and_15_out, and_16_out, and_17_out, and_18_out,
       and_19_out, and_20_out, and_21_out, and_22_out, and_23_out, and_24_out, and_25_out, and_26_out, c3,
       g0, g1, g2, g3, g4, g5, g6, g7, multiplexer_2_out, or_2_out, or_3_out, or_4_out, or_6_out, or_7_out,
       or_8_out, p0, p1, p2, p3, p4, p5, p6, p7, xnor_1_out, xnor_2_out, xnor_3_out, xnor_4_out, xnor_5_out,
       xnor_6_out, xnor_7_out, xnor_8_out, xor_2_out, xor_3_out, xor_4_out, xor_5_out, xor_6_out, xor_7_out,
       xor_8_out, xor_9_out;
  wire [0:0] and_10_out;
  wire [7:0] add, and_1_out, not_1_out, or_1_out, shifter_1_out, shifter_2_out, xor_1_out;

  assign and_1_out = a & b;  // AND_Gate and_1, 8 bits wide
  assign xor_1_out = a ^ b;  // XOR_Gate xor_1, 8 bits wide
  assign or_1_out = a | b;  // OR_Gate or_1, 8 bits wide
  xor xor_2 (xor_2_out, b[1], multiplexer_2_out);
  xor xor_3 (xor_3_out, b[2], multiplexer_2_out);
  xor xor_4 (xor_4_out, b[3], multiplexer_2_out);
  xor xor_5 (xor_5_out, b[6], multiplexer_2_out);
  xor xor_6 (xor_6_out, b[7], multiplexer_2_out);
  xor xor_7 (xor_7_out, multiplexer_2_out, b[0]);
  xor xor_8 (xor_8_out, b[4], multiplexer_2_out);
  xor xor_9 (xor_9_out, b[5], multiplexer_2_out);
  assign not_1_out = ~a;  // NOT_Gate not_1, 8 bits wide
  and and_2 (g0, a[0], xor_7_out);
  xor xor_10 (p0, a[0], xor_7_out);
  and and_3 (g1, a[1], xor_2_out);
  xor xor_11 (p1, a[1], xor_2_out);
  and and_4 (g2, a[2], xor_3_out);
  xor xor_12 (p2, a[2], xor_3_out);
  and and_5 (g3, a[3], xor_4_out);
  xor xor_13 (p3, a[3], xor_4_out);
  and and_6 (g4, a[4], xor_8_out);
  xor xor_14 (p4, a[4], xor_8_out);
  and and_7 (g5, a[5], xor_9_out);
  xor xor_15 (p5, a[5], xor_9_out);
  and and_8 (g6, a[6], xor_5_out);
  xor xor_16 (p6, a[6], xor_5_out);
  and and_9 (g7, a[7], xor_6_out);
  xor xor_17 (p7, a[7], xor_6_out);
  Shifter shifter_1 (.in(a), .\dist (3'b001), .out(shifter_1_out));
  Shifter #(.shift("lr")) shifter_2 (.in(a), .\dist (3'b001), .out(shifter_2_out));
  Multiplexer #(.select(4), .width(8), .enable("false")) multiplexer_1 (
    .in1(not_1_out), .in2(and_1_out), .in3(xor_1_out), .in4(or_1_out), .in5(add), .in6(add), .in7(a),
    .in8(b), .in9(add), .in10(add), .in11(shifter_1_out), .in12(shifter_2_out),
    .in13({{7{1'b0}}, and_10_out[0]}), .out(rddata), .sel(op));  // open: in0, in14, in15
  Multiplexer #(.select(4), .enable("false")) multiplexer_2 (
    .in5(1'b0), .in6(1'b1), .in9(1'b0), .in10(1'b1), .out(multiplexer_2_out), .sel(op));  // open: in0, in1, in2, in3, in4, in7, in8, in11, in12, in13, in14, in15
  xnor xnor_1 (xnor_1_out, a[0], b[0]);
  xnor xnor_2 (xnor_2_out, a[1], b[1]);
  xnor xnor_3 (xnor_3_out, a[2], b[2]);
  xnor xnor_4 (xnor_4_out, a[3], b[3]);
  xnor xnor_5 (xnor_5_out, a[4], b[4]);
  xnor xnor_6 (xnor_6_out, a[5], b[5]);
  xnor xnor_7 (xnor_7_out, a[6], b[6]);
  xnor xnor_8 (xnor_8_out, a[7], b[7]);
  and and_10 (and_10_out[0], xnor_1_out, xnor_2_out, xnor_3_out, xnor_4_out, xnor_5_out, xnor_6_out, xnor_7_out, xnor_8_out);
  and and_11 (and_11_out, multiplexer_2_out, p0);
  and and_12 (and_12_out, multiplexer_2_out, p0, p1);
  and and_13 (and_13_out, g0, p1);
  xor xor_18 (add[0], multiplexer_2_out, p0);
  or or_2 (or_2_out, and_11_out, g0);
  or or_3 (or_3_out, and_12_out, and_13_out, g1);
  and and_14 (and_14_out, multiplexer_2_out, p0, p1, p2);
  and and_15 (and_15_out, g0, p1, p2);
  and and_16 (and_16_out, g1, p2);
  and and_17 (and_17_out, multiplexer_2_out, p0, p1, p2, p3);
  and and_18 (and_18_out, g0, p1, p2, p3);
  and and_19 (and_19_out, g1, p2, p3);
  and and_20 (and_20_out, g2, p3);
  xor xor_19 (add[1], or_2_out, p1);
  xor xor_20 (add[2], or_3_out, p2);
  or or_4 (or_4_out, and_14_out, and_15_out, and_16_out, g2);
  or or_5 (c3, and_17_out, and_18_out, and_19_out, and_20_out, g3);
  xor xor_21 (add[3], or_4_out, p3);
  xor xor_22 (add[4], c3, p4);
  and and_21 (and_21_out, c3, p4);
  and and_22 (and_22_out, c3, p4, p5);
  and and_23 (and_23_out, g4, p5);
  or or_6 (or_6_out, and_21_out, g4);
  or or_7 (or_7_out, and_22_out, and_23_out, g5);
  and and_24 (and_24_out, c3, p4, p5, p6);
  and and_25 (and_25_out, g4, p5, p6);
  and and_26 (and_26_out, g5, p6);
  xor xor_23 (add[5], or_6_out, p5);
  xor xor_24 (add[6], or_7_out, p6);
  or or_8 (or_8_out, and_24_out, and_25_out, and_26_out, g6);
  xor xor_25 (add[7], or_8_out, p7);

  // Other names for the same wires on the sheet: s0 = add[0]; sub[7:0] = add; s1 = add[1]; s2 = add[2]; s3 = add[3];
  //   s4 = add[4]; s5 = add[5]; s6 = add[6]; s7 = add[7]
endmodule
