// Logisim project extracredit.circ as structural Verilog: 1 circuit, main circuit ledger
module ledger (
  input  [2:0] customerid,
  input  [1:0] transactiontype,
  input  [7:0] transactionamount,
  input  sysclock,
  output [1:0] transactionresult,
  output [7:0] amountremaining
);

  wire a, and_9_out, and_10_out, and_11_out, and_12_out, and_13_out, and_14_out, and_15_out, and_16_out,
       and_17_out, and_18_out, and_19_out, and_20_out, and_21_out, and_22_out, and_23_out, and_24_out,
       and_25_out, and_26_out, and_27_out, and_28_out, b, c, c3, c7, d, decoder_1_out0, decoder_1_out1,
       decoder_1_out2, decoder_1_out3, decoder_1_out4, decoder_1_out5, decoder_1_out6, decoder_1_out7, e, f,
       g, g0, g1, g2, g3, g4, g5, g6, g7, h, multiplexer_9_out, or_1_out, or_2_out, or_3_out, or_5_out,
       or_6_out, or_7_out, p0, p1, p2, p3, p4, p5, p6, p7, xor_1_out, xor_2_out, xor_3_out, xor_4_out,
       xor_5_out, xor_6_out, xor_7_out, xor_8_out;
  wire [1:0] multiplexer_3_out, multiplexer_4_out;
  wire [7:0] add, multiplexer_5_out, multiplexer_6_out, multiplexer_8_out, register_1_q, register_2_q,
       register_3_q, register_4_q, register_5_q, register_6_q, register_7_q, register_8_q, show1, show2;

  xor xor_1 (xor_1_out, multiplexer_9_out, transactionamount[0]);
  xor xor_2 (xor_2_out, transactionamount[1], multiplexer_9_out);
  xor xor_3 (xor_3_out, transactionamount[2], multiplexer_9_out);
  xor xor_4 (xor_4_out, transactionamount[3], multiplexer_9_out);
  xor xor_5 (xor_5_out, transactionamount[4], multiplexer_9_out);
  xor xor_6 (xor_6_out, transactionamount[5], multiplexer_9_out);
  xor xor_7 (xor_7_out, transactionamount[6], multiplexer_9_out);
  xor xor_8 (xor_8_out, transactionamount[7], multiplexer_9_out);
  and and_1 (g0, a, xor_1_out);
  xor xor_9 (p0, a, xor_1_out);
  and and_2 (g1, b, xor_2_out);
  xor xor_10 (p1, b, xor_2_out);
  and and_3 (g2, c, xor_3_out);
  xor xor_11 (p2, c, xor_3_out);
  and and_4 (g3, d, xor_4_out);
  xor xor_12 (p3, d, xor_4_out);
  and and_5 (g4, e, xor_5_out);
  xor xor_13 (p4, e, xor_5_out);
  and and_6 (g5, f, xor_6_out);
  xor xor_14 (p5, f, xor_6_out);
  and and_7 (g6, g, xor_7_out);
  xor xor_15 (p6, g, xor_7_out);
  and and_8 (g7, h, xor_8_out);
  xor xor_16 (p7, h, xor_8_out);
  Multiplexer #(.select(2), .width(8), .enable("false")) multiplexer_1 (
    .in0({h, g, f, e, d, c, b, a}), .in1(show2), .in2(show2), .in3(show1), .out(amountremaining),
    .sel(transactiontype));
  Multiplexer #(.select(3), .width(8), .enable("false")) multiplexer_2 (
    .in0(show1), .in1(show1), .in2(show1), .in3(show1), .in4(show1), .in5(show1), .in6(show1), .in7(show1),
    .out({h, g, f, e, d, c, b, a}), .sel(customerid));
  Multiplexer #(.width(2), .enable("false")) multiplexer_3 (
    .in0(2'b01), .in1(2'b10), .out(multiplexer_3_out), .sel(c7));
  Multiplexer #(.width(2), .enable("false")) multiplexer_4 (
    .in0(2'b11), .in1(2'b01), .out(multiplexer_4_out), .sel(c7));
  Multiplexer #(.width(8), .enable("false")) multiplexer_5 (
    .in0(add), .in1({h, g, f, e, d, c, b, a}), .out(multiplexer_5_out), .sel(c7));
  Multiplexer #(.width(8), .enable("false")) multiplexer_6 (
    .in0({h, g, f, e, d, c, b, a}), .in1(add), .out(multiplexer_6_out), .sel(c7));
  Multiplexer #(.select(2), .width(2), .enable("false")) multiplexer_7 (
    .in0(2'b00), .in1(multiplexer_3_out), .in2(multiplexer_4_out), .out(transactionresult),
    .sel(transactiontype));  // open: in3
  xor xor_17 (add[0], multiplexer_9_out, p0);
  and and_9 (and_9_out, multiplexer_9_out, p0);
  and and_10 (and_10_out, multiplexer_9_out, p0, p1);
  and and_11 (and_11_out, g0, p1);
  Multiplexer #(.select(2), .width(8), .enable("false")) multiplexer_8 (
    .in0({h, g, f, e, d, c, b, a}), .in1(multiplexer_5_out), .in2(multiplexer_6_out),
    .in3({h, g, f, e, d, c, b, a}), .out(multiplexer_8_out), .sel(transactiontype));
  or or_1 (or_1_out, and_9_out, g0);
  or or_2 (or_2_out, and_10_out, and_11_out, g1);
  and and_12 (and_12_out, multiplexer_9_out, p0, p1, p2);
  and and_13 (and_13_out, g0, p1, p2);
  and and_14 (and_14_out, g1, p2);
  and and_15 (and_15_out, multiplexer_9_out, p0, p1, p2, p3);
  and and_16 (and_16_out, g0, p1, p2, p3);
  and and_17 (and_17_out, g1, p2, p3);
  and and_18 (and_18_out, g2, p3);
  xor xor_18 (add[1], or_1_out, p1);
  or or_3 (or_3_out, and_12_out, and_13_out, and_14_out, g2);
  xor xor_19 (add[2], or_2_out, p2);
  or or_4 (c3, and_15_out, and_16_out, and_17_out, and_18_out, g3);
  Decoder #(.select(3)) decoder_1 (
    .out0(decoder_1_out0), .out1(decoder_1_out1), .out2(decoder_1_out2), .out3(decoder_1_out3),
    .out4(decoder_1_out4), .out5(decoder_1_out5), .out6(decoder_1_out6), .out7(decoder_1_out7),
    .sel(customerid), .en(1'b1));
  xor xor_20 (add[3], or_3_out, p3);
  Multiplexer #(.select(2), .enable("false")) multiplexer_9 (
    .in1(1'b0), .in2(1'b1), .out(multiplexer_9_out), .sel(transactiontype));  // open: in0, in3
  xor xor_21 (add[4], c3, p4);
  and and_19 (and_19_out, c3, p4);
  and and_20 (and_20_out, c3, p4, p5);
  and and_21 (and_21_out, g4, p5);
  or or_5 (or_5_out, and_19_out, g4);
  or or_6 (or_6_out, and_20_out, and_21_out, g5);
  and and_22 (and_22_out, c3, p4, p5, p6);
  and and_23 (and_23_out, g4, p5, p6);
  and and_24 (and_24_out, g5, p6);
  Register register_1 (.D(multiplexer_8_out), .en(decoder_1_out0), .clk(sysclock), .Q(register_1_q), .clr(1'b0));
  Register register_2 (.D(multiplexer_8_out), .en(decoder_1_out1), .clk(sysclock), .Q(register_2_q), .clr(1'b0));
  Register register_3 (.D(multiplexer_8_out), .en(decoder_1_out2), .clk(sysclock), .Q(register_3_q), .clr(1'b0));
  Register register_4 (.D(multiplexer_8_out), .en(decoder_1_out3), .clk(sysclock), .Q(register_4_q), .clr(1'b0));
  Register register_5 (.D(multiplexer_8_out), .en(decoder_1_out4), .clk(sysclock), .Q(register_5_q), .clr(1'b0));
  Register register_6 (.D(multiplexer_8_out), .en(decoder_1_out5), .clk(sysclock), .Q(register_6_q), .clr(1'b0));
  Register register_7 (.D(multiplexer_8_out), .en(decoder_1_out6), .clk(sysclock), .Q(register_7_q), .clr(1'b0));
  Register register_8 (.D(multiplexer_8_out), .en(decoder_1_out7), .clk(sysclock), .Q(register_8_q), .clr(1'b0));
  xor xor_22 (add[5], or_5_out, p5);
  xor xor_23 (add[6], or_6_out, p6);
  or or_7 (or_7_out, and_22_out, and_23_out, and_24_out, g6);
  and and_25 (and_25_out, c3, p4, p5, p6, p7);
  and and_26 (and_26_out, g4, p5, p6, p7);
  and and_27 (and_27_out, g5, p6, p7);
  and and_28 (and_28_out, g6, p7);
  xor xor_24 (add[7], or_7_out, p7);
  Multiplexer #(.select(3), .width(8), .enable("false")) multiplexer_10 (
    .in0(register_1_q), .in1(register_2_q), .in2(register_3_q), .in3(register_4_q), .in4(register_5_q),
    .in5(register_6_q), .in6(register_7_q), .in7(register_8_q), .out(show1), .sel(customerid));
  Multiplexer #(.select(3), .width(8), .enable("false")) multiplexer_11 (
    .in0(multiplexer_8_out), .in1(multiplexer_8_out), .in2(multiplexer_8_out), .in3(multiplexer_8_out),
    .in4(multiplexer_8_out), .in5(multiplexer_8_out), .in6(multiplexer_8_out), .in7(multiplexer_8_out),
    .out(show2), .sel(customerid));
  or or_8 (c7, and_25_out, and_26_out, and_27_out, and_28_out, g7);

  // Other names for the same wires on the sheet: show[7:0] = {h, g, f, e, d, c, b, a}; s0 = add[0]; sub[7:0] = add;
  //   s1 = add[1]; s2 = add[2]; s3 = add[3]; s4 = add[4]; s5 = add[5]; s6 = add[6]; s7 = add[7]
endmodule
